// Logisim project Project4.circ as structural Verilog: 15 circuits, main circuit ALU
module ALU (
  input  PcSrc,
  input  [31:0] A,
  input  [31:0] B,
  input  [1:0] ALU_Control,
  output [31:0] Result,
  output [3:0] ALU_flags
);

  wire adder_1_cout, bitselector_1_out, bitselector_2_out, bitselector_3_out, bitselector_4_out,
       bitselector_5_out, not_1_out, or_2_out, xnor_1_out, xor_1_out;
  wire [31:0] adder_1_out, and_1_out, or_1_out, subtractor_1_out;

  // Probe on A
  BitSelector #(.width(32)) bitselector_1 (.in(A), .out(bitselector_1_out), .sel({5{1'b1}}));
  // Probe on B
  BitSelector #(.width(32)) bitselector_2 (.in(B), .out(bitselector_2_out), .sel({5{1'b1}}));
  BitSelector #(.width(2)) bitselector_3 (.in(ALU_Control), .out(bitselector_3_out), .sel(1'b0));
  Adder #(.width(32)) adder_1 (.a(A), .b(B), .out(adder_1_out), .cout(adder_1_cout));  // open: cin
  Subtractor #(.width(32)) subtractor_1 (.a(A), .b(B), .out(subtractor_1_out));  // open: bin, bout
  assign and_1_out = A & B;  // AND_Gate and_1, 32 bits wide
  assign or_1_out = A | B;  // OR_Gate or_1, 32 bits wide
  BitSelector #(.width(2)) bitselector_4 (.in(ALU_Control), .out(bitselector_4_out), .sel(1'b1));
  not not_1 (not_1_out, bitselector_4_out);
  Multiplexer #(.select(2), .width(32)) multiplexer_1 (
    .in0(adder_1_out), .in1(subtractor_1_out), .in2(and_1_out), .in3(or_1_out),
    .out({ALU_flags[3], Result[30:0]}), .sel(ALU_Control));  // open: en
  BitSelector #(.width(32)) bitselector_5 (.in(adder_1_out), .out(bitselector_5_out), .sel({5{1'b1}}));
  // Probe on {ALU_flags[3], Result[30:0]}
  xor xor_1 (xor_1_out, bitselector_5_out, bitselector_1_out);
  NotExactlyOne xnor_1 (.out(xnor_1_out), .in0(bitselector_2_out), .in1(bitselector_1_out), .in2(bitselector_3_out));
  and and_2 (ALU_flags[0], adder_1_cout, not_1_out);
  or or_2 (or_2_out, Result[0], Result[1], Result[2], Result[3], Result[4], Result[5], Result[6], Result[7], Result[8], Result[9], Result[10], Result[11], Result[12], Result[13], Result[14], Result[15], Result[16], Result[17], Result[18], Result[19], Result[20], Result[21], Result[22], Result[23], Result[24], Result[25], Result[26], Result[27], Result[28], Result[29], Result[30], ALU_flags[3]);
  and and_3 (ALU_flags[1], xor_1_out, xnor_1_out, not_1_out);
  not not_2 (ALU_flags[2], or_2_out);

  assign Result[31] = ALU_flags[3];

  // Notes on the sheet:
  //   31 bit of A
  //   31 bit of B
  //   0 bit of Control
  //   Carry out bit of adder
  //   1 bit of Control
  //   31 bit of sum
  //   Glags are NZCV
endmodule

module Arm_single_cycle (
  input  Reset,
  input  CLK
);

  wire and_1_out, and_2_out, B_BL, bl, clock_1_out, control_unit_1_alusrc, control_unit_1_memtoreg,
       control_unit_1_memwrite, control_unit_1_pcsrc, control_unit_1_regwrite, Mov, Pc_t;
  wire [1:0] control_unit_1_alu_control, control_unit_1_immsrc, control_unit_1_regsrc,
       separate_instruction_1_op_26_27;
  wire [3:0] alu_1_alu_flags, multiplexer_2_out, multiplexer_3_out, multiplexer_4_out,
       separate_instruction_1__0_3, separate_instruction_1__12_15, separate_instruction_1__16_19,
       separate_instruction_1_cond_28_31, separate_instruction_1_rd_12_15;
  wire [5:0] separate_instruction_1_funct_20_25;
  wire [23:0] separate_instruction_1__0_24, separate_instruction_1_iw4_27;
  wire [31:0] adder_1_out, adder_2_out, alu_1_result, data_memory_1_out_6, extender_1_extimm,
       instruction_memory_1_rd, LR, multiplexer_1_out, multiplexer_5_out, multiplexer_6_out,
       multiplexer_7_out, multiplexer_8_out, multiplexer_9_out, multiplexer_10_out, multiplexer_11_out, PC,
       PC_q, r0, r1, r2, r3, r4, r5, r6, register_file_1_value_at_reg_addr_1,
       register_file_1_value_at_reg_addr_2, sp, subtractor_1_out;

  // Probe on adder_1_out
  // Probe on multiplexer_10_out
  // Probe on multiplexer_1_out
  Multiplexer #(.width(32), .disabled(0), .enable("false")) multiplexer_1 (
    .in0(adder_1_out), .in1(multiplexer_10_out), .out(multiplexer_1_out), .sel(control_unit_1_pcsrc));
  Register #(.width(32)) u_PC (.D(multiplexer_1_out), .Q(PC_q), .clk(clock_1_out), .clr(Reset));  // open: en
  // Probe on PC_q
  // Probe on PC_q
  // Probe on adder_1_out
  Adder #(.width(32)) adder_1 (.a(PC_q), .b(32'h4), .out(adder_1_out));  // open: cin, cout
  // Probe on r0
  // Probe on instruction_memory_1_rd
  // Probe on r1
  // Probe on separate_instruction_1_cond_28_31
  Instruction_Memory instruction_memory_1 (.Address(PC_q), .RD(instruction_memory_1_rd));
  Clock clock_1 (.out(clock_1_out));
  // Probe on r2
  // Probe on separate_instruction_1_op_26_27
  // Probe on separate_instruction_1_funct_20_25
  // Probe on r3
  // Probe on sp
  // Probe on separate_instruction_1_rd_12_15
  // Probe on r4
  // Probe on LR
  separate_instruction separate_instruction_1 (
    .IW(instruction_memory_1_rd), .Cond_28_31(separate_instruction_1_cond_28_31),
    .OP_26_27(separate_instruction_1_op_26_27), .Funct_20_25(separate_instruction_1_funct_20_25),
    .Rd_12_15(separate_instruction_1_rd_12_15), ._16_19(separate_instruction_1__16_19),
    ._0_3(separate_instruction_1__0_3), ._12_15(separate_instruction_1__12_15),
    ._0_24(separate_instruction_1__0_24), .Mov(Mov), .Iw4_27(separate_instruction_1_iw4_27), .IsBL(bl),
    .updating_pc(Pc_t));
  // Probe on adder_2_out
  // Probe on r5
  // Probe on separate_instruction_1_funct_20_25
  // Probe on separate_instruction_1__16_19
  // Probe on separate_instruction_1__0_3
  // Probe on separate_instruction_1__12_15
  Adder #(.width(32)) adder_2 (.a(adder_1_out), .b(32'h4), .out(adder_2_out));  // open: cin, cout
  // Probe on PC
  Multiplexer #(.width(4), .disabled(0), .enable("false")) multiplexer_2 (
    .in0(separate_instruction_1__16_19), .in1(4'b1111), .out(multiplexer_2_out),
    .sel(control_unit_1_regsrc[0]));
  // Probe on multiplexer_7_out
  // Probe on r6
  // Probe on control_unit_1_regsrc
  Multiplexer #(.width(4), .disabled(0), .enable("false")) multiplexer_3 (
    .in0(separate_instruction_1__0_3), .in1(separate_instruction_1__12_15), .out(multiplexer_3_out),
    .sel(control_unit_1_regsrc[1]));
  // Probe on multiplexer_2_out
  // Probe on multiplexer_3_out
  // Probe on nothing
  // Probe on multiplexer_4_out
  Multiplexer #(.width(4), .disabled(0), .enable("false")) multiplexer_4 (
    .in0(separate_instruction_1__12_15), .in1(4'b1110), .out(multiplexer_4_out), .sel(bl));
  // Probe on multiplexer_5_out
  Multiplexer #(.width(32), .disabled(0), .enable("false")) multiplexer_5 (
    .in0(adder_2_out), .in1(PC_q), .out(multiplexer_5_out), .sel(and_1_out));
  and and_1 (and_1_out, Pc_t, Mov);
  Multiplexer #(.width(32), .disabled(0), .enable("false")) multiplexer_6 (
    .in0(multiplexer_7_out), .in1(adder_2_out), .out(multiplexer_6_out), .sel(bl));
  // Probe on multiplexer_6_out
  Multiplexer #(.width(32), .disabled(0), .enable("false")) multiplexer_7 (
    .in0(multiplexer_10_out), .in1(multiplexer_9_out), .out(multiplexer_7_out), .sel(Mov));
  // Probe on multiplexer_10_out
  Register_File register_file_1 (
    .Register_Address_1(multiplexer_2_out), .Register_Address_2(multiplexer_3_out),
    .Write_Data(multiplexer_6_out), .r15(multiplexer_5_out), .RESET(Reset),
    .Write_enable(control_unit_1_regwrite), .write_address(multiplexer_4_out), .CLK(clock_1_out),
    .Value_at_reg_addr_1(register_file_1_value_at_reg_addr_1),
    .Value_at_reg_addr_2(register_file_1_value_at_reg_addr_2), .r0(r0), .r1(r1), .LR(LR), .PC(PC), .SP(sp),
    .r4(r4), .r3(r3), .r2(r2), .R6(r6), .R5(r5));
  // Probe on multiplexer_6_out
  // Probe on multiplexer_9_out
  Control_Unit control_unit_1 (
    .RD(separate_instruction_1_rd_12_15), .OP(separate_instruction_1_op_26_27),
    .Funct(separate_instruction_1_funct_20_25), .Iw4_27(separate_instruction_1_iw4_27),
    .Cond(separate_instruction_1_cond_28_31), .ALU_FLags(alu_1_alu_flags),
    .MemToreg(control_unit_1_memtoreg), .ALUsrc(control_unit_1_alusrc), .PCSrc(control_unit_1_pcsrc),
    .Immsrc(control_unit_1_immsrc), .RegSrc(control_unit_1_regsrc), .Alu_Control(control_unit_1_alu_control),
    .RegWrite(control_unit_1_regwrite), .memWrite(control_unit_1_memwrite), .CLK(clock_1_out), .branch(B_BL));
  Extender extender_1 (
    .ImmSrc(control_unit_1_immsrc), .Bits_0_23(separate_instruction_1__0_24), .ExtImm(extender_1_extimm));
  // Probe on register_file_1_value_at_reg_addr_1
  // Probe on register_file_1_value_at_reg_addr_2
  // Probe on extender_1_extimm
  Multiplexer #(.width(32), .disabled(0), .enable("false")) multiplexer_8 (
    .in0(register_file_1_value_at_reg_addr_1), .in1({32{1'b0}}), .out(multiplexer_8_out), .sel(Mov));
  // Probe on multiplexer_9_out
  Multiplexer #(.width(32), .disabled(0), .enable("false")) multiplexer_9 (
    .in0(register_file_1_value_at_reg_addr_2), .in1(extender_1_extimm), .out(multiplexer_9_out),
    .sel(control_unit_1_alusrc));
  ALU alu_1 (
    .A(multiplexer_8_out), .B(multiplexer_9_out), .Result(alu_1_result),
    .ALU_Control(control_unit_1_alu_control), .ALU_flags(alu_1_alu_flags), .PcSrc(control_unit_1_pcsrc));
  // Probe on alu_1_result
  // Probe on multiplexer_10_out
  Data_memory data_memory_1 (
    .clk(clock_1_out), .Write_Enable(control_unit_1_memwrite), .Address(alu_1_result),
    .wd(register_file_1_value_at_reg_addr_2), .out_6(data_memory_1_out_6));  // open: Reset
  Multiplexer #(.width(32), .disabled(0), .enable("false")) multiplexer_10 (
    .in0(multiplexer_11_out), .in1(subtractor_1_out), .out(multiplexer_10_out), .sel(and_2_out));
  // Probe on data_memory_1_out_6
  and and_2 (and_2_out, ~B_BL, Pc_t);  // AND_Gate
  Subtractor #(.width(32)) subtractor_1 (.a(multiplexer_11_out), .b(32'h4), .out(subtractor_1_out));  // open: bin, bout
  // Probe on subtractor_1_out
  Multiplexer #(.width(32), .disabled(0), .enable("false")) multiplexer_11 (
    .in0(alu_1_result), .in1(data_memory_1_out_6), .out(multiplexer_11_out), .sel(control_unit_1_memtoreg));

  // Notes on the sheet:
  //   pc +8
  //   Note: must left fist the immediat before signextendign for branch
  //   Write Data
  //   This is for MOV pc LR so that it return to the right direction
  //   Read Data
endmodule

module Data_memory (
  input  clk,
  input  Write_Enable,
  input  Reset,
  input  [31:0] Address,
  input  [31:0] wd,
  output [31:0] out_6
);

  wire not_1_out;

  // Probe on Address
  // Probe on wd
  RAM #(.dataWidth(32), .bus("separate")) ram_1 (
    .addr(Address[9:2]), .din(wd), .data(out_6), .str(Write_Enable), .sel(1'b1), .clk(clk), .ld(not_1_out),
    .clr(Reset));
  not not_1 (not_1_out, Write_Enable);
  // Probe on out_6

  // Notes on the sheet:
  //   Decimal value
  //   Sepearete load and store ports
endmodule

module Instruction_Memory (
  input  [31:0] Address,
  output [31:0] RD
);

  // Probe on Address
  ROM #(.dataWidth(32)) rom_1 (.addr(Address[9:2]), .data(RD), .sel(1'b1));
  // Probe on RD

  // Notes on the sheet:
  //   contents of rom_1 (hex, n*v repeats v):
  //   e3a0000b eb000000 eafffffe e3500000 a00000c e3500001 a00000a e3a02000 e3a01001 e3a03000 e3a04001
  //   e1510000 a000004 e0832004 e1a03004 e1a04002 e2811001 eafffff8 e1a00002 e1a0f00e
endmodule

module Register_File (
  input  [3:0] Register_Address_1,
  input  [3:0] Register_Address_2,
  input  [31:0] Write_Data,
  input  [31:0] r15,
  input  RESET,
  input  Write_enable,
  input  [3:0] write_address,
  input  CLK,
  output [31:0] Value_at_reg_addr_1,
  output [31:0] r0,
  output [31:0] r1,
  output [31:0] r2,
  output [31:0] r3,
  output [31:0] r4,
  output [31:0] R5,
  output [31:0] R6,
  output [31:0] LR,
  output [31:0] SP,
  output [31:0] PC,
  output [31:0] Value_at_reg_addr_2
);

  wire decoder_1_out0, decoder_1_out1, decoder_1_out2, decoder_1_out3, decoder_1_out4, decoder_1_out5,
       decoder_1_out6, decoder_1_out7, decoder_1_out8, decoder_1_out9, decoder_1_out10, decoder_1_out11,
       decoder_1_out12, decoder_1_out13, decoder_1_out14, decoder_1_out15;
  wire [31:0] r7_q, r8_q, r9_q, r10_q, r11_q, r12_q;

  Decoder_part #(.select(4), .disabled(0)) decoder_1 (
    .out0(decoder_1_out0), .out1(decoder_1_out1), .out2(decoder_1_out2), .out3(decoder_1_out3),
    .out4(decoder_1_out4), .out5(decoder_1_out5), .out6(decoder_1_out6), .out7(decoder_1_out7),
    .out8(decoder_1_out8), .out9(decoder_1_out9), .out10(decoder_1_out10), .out11(decoder_1_out11),
    .out12(decoder_1_out12), .out13(decoder_1_out13), .out14(decoder_1_out14), .out15(decoder_1_out15),
    .sel(write_address), .en(Write_enable));
  // Probe on Write_Data
  Register #(.width(32)) u_r0 (.D(Write_Data), .en(decoder_1_out0), .Q(r0), .clk(CLK), .clr(RESET));
  Register #(.width(32)) u_r1 (.D(Write_Data), .en(decoder_1_out1), .Q(r1), .clk(CLK), .clr(RESET));
  // Probe on r1
  Register #(.width(32)) u_r2 (.D(Write_Data), .en(decoder_1_out2), .Q(r2), .clk(CLK), .clr(RESET));
  // Probe on r2
  Register #(.width(32)) u_r3 (.D(Write_Data), .en(decoder_1_out3), .Q(r3), .clk(CLK), .clr(RESET));
  // Probe on r3
  Register #(.width(32)) u_r4 (.D(Write_Data), .en(decoder_1_out4), .Q(r4), .clk(CLK), .clr(RESET));
  // Probe on r4
  Register #(.width(32)) u_r5 (.D(Write_Data), .en(decoder_1_out5), .Q(R5), .clk(CLK), .clr(RESET));
  // Probe on R5
  Register #(.width(32)) u_r6 (.D(Write_Data), .en(decoder_1_out6), .Q(R6), .clk(CLK), .clr(RESET));
  // Probe on R6
  Register #(.width(32)) r7 (.D(Write_Data), .en(decoder_1_out7), .Q(r7_q), .clk(CLK), .clr(RESET));
  // Probe on r7_q
  Register #(.width(32)) r8 (.D(Write_Data), .en(decoder_1_out8), .Q(r8_q), .clk(CLK), .clr(RESET));
  // Probe on r8_q
  Register #(.width(32)) r9 (.D(Write_Data), .en(decoder_1_out9), .Q(r9_q), .clk(CLK), .clr(RESET));
  // Probe on r9_q
  Register #(.width(32)) r10 (.D(Write_Data), .en(decoder_1_out10), .Q(r10_q), .clk(CLK), .clr(RESET));
  // Probe on r10_q
  Register #(.width(32)) r11 (.D(Write_Data), .en(decoder_1_out11), .Q(r11_q), .clk(CLK), .clr(RESET));
  // Probe on r11_q
  Register #(.width(32)) r12 (.D(Write_Data), .en(decoder_1_out12), .Q(r12_q), .clk(CLK), .clr(RESET));
  // Probe on r12_q
  Register #(.width(32)) r13 (.D(Write_Data), .en(decoder_1_out13), .Q(SP), .clk(CLK), .clr(RESET));
  // Probe on SP
  Register #(.width(32)) r14 (.D(Write_Data), .en(decoder_1_out14), .Q(LR), .clk(CLK), .clr(RESET));
  // Probe on LR
  // Probe on r15
  // Probe on nothing
  // Probe on nothing
  // Probe on nothing
  Multiplexer #(.select(4), .width(32), .disabled(0), .enable("false")) multiplexer_1 (
    .in0(r0), .in1(r1), .in2(r2), .in3(r3), .in4(r4), .in5(R5), .in6(R6), .in7(r7_q), .in8(r8_q), .in9(r9_q),
    .in10(r10_q), .in11(r11_q), .in12(r12_q), .in13(SP), .in14(LR), .in15(r15), .out(Value_at_reg_addr_1),
    .sel(Register_Address_1));
  Multiplexer #(.select(4), .width(32), .disabled(0), .enable("false")) multiplexer_2 (
    .in0(r0), .in1(r1), .in2(r2), .in3(r3), .in4(r4), .in5(R5), .in6(R6), .in7(r7_q), .in8(r8_q), .in9(r9_q),
    .in10(r10_q), .in11(r11_q), .in12(r12_q), .in13(SP), .in14(LR), .in15(r15), .out(Value_at_reg_addr_2),
    .sel(Register_Address_2));
  // Probe on Value_at_reg_addr_1
  // Probe on Value_at_reg_addr_2

  assign PC = r15;
endmodule

module Test_Reg_File (
  input  D,
  input  D_2,
  input  [3:0] D_3,
  input  [3:0] D_4,
  input  D_5,
  input  [3:0] D_6,
  input  [31:0] D_7,
  input  [31:0] D_8,
  output [31:0] out_9,
  output [31:0] out_10
);

  // Probe on D_3
  // Probe on D_6
  // Probe on D_7
  Register_File register_file_1 (
    .Register_Address_1(D_3), .Register_Address_2(D_4), .Write_Data(D_7), .r15(D_8), .RESET(D_2),
    .Write_enable(D_5), .write_address(D_6), .CLK(D), .Value_at_reg_addr_1(out_9),
    .Value_at_reg_addr_2(out_10));  // open: r0, r1, LR, PC, SP, r4, r3, r2, R6, R5
  // Probe on out_9
  // Probe on out_10
endmodule

module Main_Decoder (
  input  [23:0] Iw4_27,
  input  [1:0] OP,
  input  [5:0] Funct,
  output out_4,
  output Branch,
  output Mem_To_Reg,
  output Mem_W,
  output Alu_Src,
  output [1:0] Imm_Src,
  output Reg_W,
  output [1:0] RegSrc,
  output ALU_OP
);

  wire B_out, BL_out, BX_out, comparator_1_eq, DP_Imm_out, Dp_Reg_out, STR_out;

  Comparator #(.width(24)) comparator_1 (.a(Iw4_27), .b(24'h12fff1), .eq(comparator_1_eq));  // open: gt, lt
  and Dp_Reg (Dp_Reg_out, ~OP[0], ~OP[1], ~Funct[5]);  // AND_Gate
  and DP_Imm (DP_Imm_out, ~OP[0], ~OP[1], Funct[5]);  // AND_Gate
  and STR (STR_out, OP[0], ~OP[1], ~Funct[0]);  // AND_Gate
  and LDR (Mem_To_Reg, OP[0], ~OP[1], Funct[0]);  // AND_Gate
  and B (B_out, ~OP[0], ~Funct[4], OP[1]);  // AND_Gate
  and BL (BL_out, ~OP[0], OP[1], Funct[4]);  // AND_Gate
  buf BX (BX_out, comparator_1_eq);  // AND_Gate
  or or_1 (out_4, B_out, BL_out);
  or or_2 (Branch, BL_out, B_out, BX_out);
  or or_3 (Alu_Src, DP_Imm_out, STR_out, BL_out, Mem_To_Reg, B_out, BX_out);
  or or_4 (Imm_Src[0], STR_out, Mem_To_Reg);
  or or_5 (Imm_Src[1], B_out, BL_out);
  or or_6 (Reg_W, Dp_Reg_out, DP_Imm_out, BL_out, Mem_To_Reg);
  or or_7 (RegSrc[0], BL_out, B_out);
  or or_8 (RegSrc[1], STR_out, Mem_To_Reg);
  or or_9 (ALU_OP, Dp_Reg_out, DP_Imm_out);
  or or_10 (Mem_W, STR_out, BL_out);

  // Notes on the sheet:
  //   And gate for first row
  //   STR
  //   STR
endmodule

module ALU_Decoder (
  input  ALU_Op,
  input  [5:0] Funct,
  output [1:0] ALUControl,
  output [1:0] FlagW,
  output NoWrite
);

  wire ADD_1_out, AND_0_out, AND_1_out, Mov_0_out, OR_0_out, OR_1_out, Sub_0_out, Sub_1_out;

  // AND_Gate Add_0 has open pins: in0=ALU_Op, in1=Funct[4], in2=Funct[3], in3=Funct[2], in4=Funct[1], in5=Funct[0], out=open
  and ADD_1 (ADD_1_out, ALU_Op, ~Funct[4], Funct[3], ~Funct[2], ~Funct[1], Funct[0]);  // AND_Gate
  and Sub_0 (Sub_0_out, ALU_Op, ~Funct[4], ~Funct[3], Funct[2], ~Funct[1], ~Funct[0]);  // AND_Gate
  and Sub_1 (Sub_1_out, ALU_Op, ~Funct[4], ~Funct[3], Funct[2], ~Funct[1], Funct[0]);  // AND_Gate
  and AND_0 (AND_0_out, ALU_Op, ~Funct[4], ~Funct[3], ~Funct[2], ~Funct[1], ~Funct[0]);  // AND_Gate
  and AND_1 (AND_1_out, ALU_Op, ~Funct[4], ~Funct[3], ~Funct[2], ~Funct[1], Funct[0]);  // AND_Gate
  and OR_0 (OR_0_out, ALU_Op, Funct[4], Funct[3], ~Funct[2], ~Funct[1], ~Funct[0]);  // AND_Gate
  and OR_1 (OR_1_out, ALU_Op, Funct[4], Funct[3], ~Funct[2], ~Funct[1], Funct[0]);  // AND_Gate
  and cmp_0 (NoWrite, ALU_Op, ~Funct[1], Funct[2], ~Funct[3], Funct[4], Funct[0]);  // AND_Gate
  and Mov_0 (Mov_0_out, ~Funct[0], Funct[1], ~Funct[2], Funct[3], Funct[4], ALU_Op);  // AND_Gate
  or or_1_dup2 (ALUControl[0], Sub_0_out, Sub_1_out, OR_0_out, OR_1_out, NoWrite);  // OR_Gate
  or or_2 (ALUControl[1], AND_0_out, AND_1_out, OR_0_out, OR_1_out);  // OR_Gate
  or or_3 (FlagW[0], ADD_1_out, Sub_1_out, NoWrite);
  or or_4 (FlagW[1], ADD_1_out, Sub_1_out, AND_1_out, OR_1_out, NoWrite);

  // Notes on the sheet:
  //   DP REG
endmodule

module Condition_Logic (
  input  PCS,
  input  RegW,
  input  No_Write,
  input  MemW,
  input  [1:0] FlagW,
  input  [3:0] Cond,
  input  [3:0] ALU_Flags,
  input  CLK,
  output PCSrc,
  output RegWrite,
  output MemWrite
);

  wire condition_check_1_con_execution;
  wire [1:0] and_1_out, bit_extender_1_out, register_1_q, register_2_q;

  Register #(.width(2)) register_1 (.D(ALU_Flags[3:2]), .Q(register_1_q), .clk(CLK), .clr(and_1_out[1]));  // open: en
  Register #(.width(2)) register_2 (.D(ALU_Flags[1:0]), .Q(register_2_q), .clk(CLK), .clr(and_1_out[0]));  // open: en
  // Probe on register_2_q
  assign and_1_out = FlagW & bit_extender_1_out;  // AND_Gate and_1, 2 bits wide
  assign bit_extender_1_out = {{1{1'b0}}, condition_check_1_con_execution};  // Bit_Extender bit_extender_1
  Condition_check condition_check_1 (
    .Cond(Cond), .Flags3_2(register_1_q), .Flags1_0(register_2_q),
    .CON_EXECUTION(condition_check_1_con_execution));
  and and_2 (PCSrc, PCS, condition_check_1_con_execution);
  and and_3 (RegWrite, RegW, ~No_Write, condition_check_1_con_execution);  // AND_Gate
  and and_4 (MemWrite, MemW, condition_check_1_con_execution);
endmodule

module PC_Logic (
  input  [3:0] Rd,
  input  RegW,
  input  Branch,
  output PCS
);

  wire and_1_out, comparator_1_eq;

  Comparator #(.width(4)) comparator_1 (.a(Rd), .b(4'b1111), .eq(comparator_1_eq));  // open: gt, lt
  and and_1 (and_1_out, comparator_1_eq, RegW);
  or or_1 (PCS, and_1_out, Branch);
endmodule

module Condition_check (
  input  [3:0] Cond,
  input  [1:0] Flags3_2,
  input  [1:0] Flags1_0,
  output CON_EXECUTION
);

  wire AL_out, EQ_out, LT_out, NE_out, or_1_out;

  or or_1 (or_1_out, Flags3_2[1], Flags1_0[0]);
  and EQ (EQ_out, ~Cond[0], ~Cond[1], ~Cond[2], ~Cond[3], Flags3_2[0]);  // AND_Gate
  and NE (NE_out, Cond[0], ~Cond[1], ~Cond[2], ~Cond[3], ~Flags3_2[0]);  // AND_Gate
  and AL (AL_out, ~Cond[0], Cond[1], Cond[2], Cond[3]);  // AND_Gate
  and LT (LT_out, Cond[0], Cond[1], ~Cond[2], Cond[3], or_1_out);  // AND_Gate
  or or_2 (CON_EXECUTION, EQ_out, NE_out, AL_out, LT_out);

  // Notes on the sheet:
  //   NZ
  //   CV
  //   NZCV
endmodule

module Decoder (
  input  [3:0] RD,
  input  [1:0] op,
  input  [5:0] Funct5_0,
  input  [23:0] Iw4_27,
  output out_5,
  output branch,
  output out_7,
  output out_8,
  output out_9,
  output out_10,
  output [1:0] out_11,
  output [1:0] out_12,
  output [1:0] AluControl,
  output [1:0] FlagW,
  output NoWrite
);

  wire main_decoder_1_alu_op, main_decoder_1_branch;

  Main_Decoder main_decoder_1 (
    .OP(op), .Funct(Funct5_0), .Branch(main_decoder_1_branch), .Mem_To_Reg(out_9), .Mem_W(out_8),
    .Alu_Src(out_10), .Imm_Src(out_11), .Reg_W(out_7), .RegSrc(out_12), .ALU_OP(main_decoder_1_alu_op),
    .Iw4_27(Iw4_27), .out_4(branch));
  ALU_Decoder alu_decoder_1 (
    .ALU_Op(main_decoder_1_alu_op), .Funct(Funct5_0), .ALUControl(AluControl), .FlagW(FlagW),
    .NoWrite(NoWrite));
  PC_Logic pc_logic_1 (.Rd(RD), .RegW(out_7), .Branch(main_decoder_1_branch), .PCS(out_5));
endmodule

module separate_instruction (
  input  [31:0] IW,
  output [3:0] Cond_28_31,
  output [1:0] OP_26_27,
  output [5:0] Funct_20_25,
  output Mov,
  output [3:0] Rd_12_15,
  output IsBL,
  output [3:0] _16_19,
  output [3:0] _0_3,
  output [3:0] _12_15,
  output updating_pc,
  output [23:0] _0_24,
  output [23:0] Iw4_27
);

  Comparator #(.width(4)) comparator_1 (.a(IW[15:12]), .b(4'b1111), .eq(updating_pc));  // open: gt, lt
  and and_1 (IsBL, ~IW[26], IW[27], IW[24]);  // AND_Gate
  and and_2 (Mov, ~IW[26], ~IW[27], IW[21], ~IW[22], IW[23], IW[24]);  // AND_Gate

  assign _0_3 = IW[3:0];
  assign _0_24 = IW[23:0];
  assign _12_15 = IW[15:12];
  assign _16_19 = IW[19:16];
  assign Cond_28_31 = IW[31:28];
  assign Funct_20_25 = IW[25:20];
  assign Iw4_27 = IW[27:4];
  assign OP_26_27 = IW[27:26];
  assign Rd_12_15 = IW[15:12];

  // Notes on the sheet:
  //   bits 16 -19
  //   bit 0-3
  //   bits 12-15
  //   Bits 0-23
endmodule

module Extender (
  input  [1:0] ImmSrc,
  input  [23:0] Bits_0_23,
  output [31:0] ExtImm
);

  wire [23:0] demultiplexer_1_out0, demultiplexer_1_out1, demultiplexer_1_out2, demultiplexer_1_out3;
  wire [31:0] bit_extender_1_out, bit_extender_2_out;

  Demultiplexer #(.select(2), .width(24), .disabled(0), .enable("false")) demultiplexer_1 (
    .out0(demultiplexer_1_out0), .out1(demultiplexer_1_out1), .out2(demultiplexer_1_out2),
    .out3(demultiplexer_1_out3), .in(Bits_0_23), .sel(ImmSrc));
  // Probe on demultiplexer_1_out2
  // Probe on demultiplexer_1_out0
  // Probe on {{7{demultiplexer_1_out2[23]}}, demultiplexer_1_out2[22:0], 2'b00}
  assign bit_extender_1_out = {{20{1'b0}}, demultiplexer_1_out1[11:0]};  // Bit_Extender bit_extender_1
  assign bit_extender_2_out = {{24{1'b0}}, demultiplexer_1_out0[7:0]};  // Bit_Extender bit_extender_2
  Multiplexer #(.select(2), .width(32), .disabled(0), .enable("false")) multiplexer_1 (
    .in0(bit_extender_2_out), .in1(bit_extender_1_out),
    .in2({{7{demultiplexer_1_out2[23]}}, demultiplexer_1_out2[22:0], 2'b00}), .out(ExtImm), .sel(ImmSrc));  // open: in3
  // Probe on ExtImm
endmodule

module Control_Unit (
  input  CLK,
  input  [3:0] RD,
  input  [1:0] OP,
  input  [23:0] Iw4_27,
  input  [5:0] Funct,
  input  [3:0] Cond,
  input  [3:0] ALU_FLags,
  output MemToreg,
  output ALUsrc,
  output PCSrc,
  output [1:0] Immsrc,
  output [1:0] RegSrc,
  output [1:0] Alu_Control,
  output RegWrite,
  output branch,
  output memWrite
);

  wire decoder_1_nowrite, decoder_1_out_5, decoder_1_out_7, decoder_1_out_8;
  wire [1:0] decoder_1_flagw;

  Decoder decoder_1 (
    .RD(RD), .op(OP), .Funct5_0(Funct), .out_5(decoder_1_out_5), .out_7(decoder_1_out_7),
    .out_8(decoder_1_out_8), .out_9(MemToreg), .out_10(ALUsrc), .out_11(Immsrc), .out_12(RegSrc),
    .AluControl(Alu_Control), .FlagW(decoder_1_flagw), .NoWrite(decoder_1_nowrite), .Iw4_27(Iw4_27),
    .branch(branch));
  Condition_Logic condition_logic_1 (
    .PCS(decoder_1_out_5), .RegW(decoder_1_out_7), .MemW(decoder_1_out_8), .FlagW(decoder_1_flagw),
    .Cond(Cond), .ALU_Flags(ALU_FLags), .PCSrc(PCSrc), .RegWrite(RegWrite), .MemWrite(memWrite),
    .No_Write(decoder_1_nowrite), .CLK(CLK));
endmodule
